# Fritzing sketch Octopus (saved by Fritzing 0.9.5d)
circuit board: 12.641cm x 7.87964cm
breadboards: 1

parts:
  part = Raspberry Pi Pico
  part_2 = Grove OLED 128x96
  S1 = SWITCH-MOMENTARY-2 [package=tactile-pth-12mm]
  S2 = SWITCH-MOMENTARY-2 [package=tactile-pth-12mm]
  S3 = SWITCH-MOMENTARY-2 [package=tactile-pth-12mm]
  S4 = SWITCH-MOMENTARY-2 [package=tactile-pth-12mm]
  S5 = SWITCH-MOMENTARY-2 [package=tactile-pth-12mm]
  S6 = SWITCH-MOMENTARY-2 [package=tactile-pth-12mm]
  S7 = SWITCH-MOMENTARY-2 [package=tactile-pth-12mm]
  S8 = SWITCH-MOMENTARY-2 [package=tactile-pth-12mm]
  S9 = SWITCH-MOMENTARY-2 [package=tactile-pth-12mm]
  S10 = SWITCH-MOMENTARY-2 [package=tactile-pth-12mm]
  R1 = Resistor [tolerance=±5% resistance=220 package=THT]

nets:
  N1: part.pin_3, part.pin_8, part.pin_13, part.pin_18, part.pin_23, part.pin_28, part.pin_33, part.pin_38, part.pin_42, part_2.SCL
  N2: part.pin_6, S10.2
  N3: part.pin_9, S3.2
  N4: part.pin_10, S4.2
  N5: part.pin_11, S2.2
  N6: part.pin_12, S5.2
  N7: part.pin_14, part_2.VCC
  N8: part.pin_15, part_2.GND
  N9: part.pin_21, S6.2
  N10: part.pin_22, S7.2
  N11: part.pin_24, S9.2
  N12: part.pin_25, S8.2
  N13: part.pin_26, S1.2
  N14: part.pin_36, part_2.SDA, R1.Pin_0
  N15: S1.1, S2.1, S3.1, S4.1, S5.1, S6.1, S7.1, S8.1, S9.1, S10.1, R1.Pin_1

notes:
  Octopus 1.0

custom parts:
  Raspberry Pi Pico: Raspberry Pi Pico. Based around the RP2040 microcontroller the Pico is a low cost microcontroller device bringing Raspberry Pi quality, cost, and easy of use to the microcontroller space. Jan 2021, Split part in to two versions: tht (this one) and SMD. This one will drill holes for a .1 in header in pcb to allow plugging in the module as well as providing pads to solder the module to the top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
