# Fritzing sketch Octopusv2 (saved by Fritzing 0.9.5d)
circuit board: 6.96584cm x 6.78449cm
breadboards: 1

parts:
  S2 = SWITCH-MOMENTARY-2 [package=tactile-pth-12mm]
  S3 = SWITCH-MOMENTARY-2 [package=tactile-pth-12mm]
  S4 = SWITCH-MOMENTARY-2 [package=tactile-pth-12mm]
  Mod1 = Raspberry Pi Pico
  S5 = SWITCH-MOMENTARY-2 [package=tactile-pth-12mm]
  S6 = SWITCH-MOMENTARY-2 [package=tactile-pth-12mm]
  S7 = SWITCH-MOMENTARY-2 [package=tactile-pth-12mm]
  R1 = Resistor [tolerance=±5% resistance=220 package=THT]
  R2 = Resistor [tolerance=±5% resistance=220 package=THT]
  R3 = Resistor [tolerance=±5% resistance=220 package=THT]
  R4 = Resistor [tolerance=±5% resistance=220 package=THT]
  R5 = Resistor [tolerance=±5% resistance=220 package=THT]
  R6 = Resistor [tolerance=±5% resistance=220 package=THT]

nets:
  N1: S2.1, Mod1.pin_19, R4.Pin_0
  N2: S2.2, S3.2, S4.2, Mod1.pin_36, S5.2, S6.2, S7.2
  N3: S3.1, Mod1.pin_12, R3.Pin_0
  N4: S4.1, Mod1.pin_4, R1.Pin_1
  N5: Mod1.pin_3, Mod1.pin_8, Mod1.pin_18, Mod1.pin_23, Mod1.pin_42, R1.Pin_0, R2.Pin_0, R3.Pin_1, R4.Pin_1, R5.Pin_1, R6.Pin_1
  N6: Mod1.pin_5, S7.1, R2.Pin_1
  N7: Mod1.pin_14, S5.1, R6.Pin_0
  N8: Mod1.pin_20, S6.1, R5.Pin_0

custom parts:
  Raspberry Pi Pico: Raspberry Pi Pico. Based around the RP2040 microcontroller the Pico is a low cost microcontroller device bringing Raspberry Pi quality, cost, and easy of use to the microcontroller space. Jan 2021, Split part in to two versions: tht (this one) and SMD. This one will drill holes for a .1 in header in pcb to allow plugging in the module as well as providing pads to solder the module to the top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
